// Logisim project CPU.circ as structural Verilog: 15 circuits, main circuit main
module main (
  input  in_1,
  input  in_2,
  input  in_3,
  input  in_4,
  input  in_5,
  input  in_6,
  input  in_7,
  input  in_8,
  input  in_9,
  input  in_10,
  input  in_11,
  input  in_12,
  input  in_13,
  input  in_14,
  input  in_15,
  input  in_16,
  input  in_17
);

  wire n8_bit_selector_1_out_0, n8_bit_selector_1_out_1, n8_bit_selector_1_out_2, n8_bit_selector_1_out_3,
       n8_bit_selector_1_out_4, n8_bit_selector_1_out_5, n8_bit_selector_1_out_6, n8_bit_selector_1_out_7;

  _8_Bit_Selector u_8_bit_selector_1 (
    .B_7(in_1), .B_6(in_2), .B_5(in_3), .B_4(in_4), .B_3(in_5), .B_2(in_6), .B_1(in_7), .B_0(in_8),
    .A_7(in_9), .A_6(in_10), .A_5(in_11), .A_4(in_12), .A_3(in_13), .A_2(in_14), .A_1(in_15), .A_0(in_16),
    .Selector(in_17), .Out_7(n8_bit_selector_1_out_7), .Out_6(n8_bit_selector_1_out_6),
    .Out_5(n8_bit_selector_1_out_5), .Out_4(n8_bit_selector_1_out_4), .Out_3(n8_bit_selector_1_out_3),
    .Out_2(n8_bit_selector_1_out_2), .Out_1(n8_bit_selector_1_out_1), .Out_0(n8_bit_selector_1_out_0));
  LED led_1 (.in(n8_bit_selector_1_out_7));
  LED led_2 (.in(n8_bit_selector_1_out_5));
  LED led_3 (.in(n8_bit_selector_1_out_6));
  LED led_4 (.in(n8_bit_selector_1_out_4));
  LED led_5 (.in(n8_bit_selector_1_out_2));
  LED led_6 (.in(n8_bit_selector_1_out_3));
  LED led_7 (.in(n8_bit_selector_1_out_1));
  LED led_8 (.in(n8_bit_selector_1_out_0));
endmodule

module adder (
  input  _1,
  input  _2,
  input  C_in,
  output A_out,
  output C_out
);

  wire and_1_out, and_2_out, buffer_1_out, or_1_out, xor_1_out, xor_2_out;

  buf buffer_1 (buffer_1_out, C_in);
  and and_1 (and_1_out, _2, _1);
  xor xor_1 (xor_1_out, _1, _2);
  xor xor_2 (xor_2_out, xor_1_out, buffer_1_out);
  or or_1 (or_1_out, and_1_out, and_2_out);
  and and_2 (and_2_out, xor_1_out, buffer_1_out);
  buf buffer_2 (C_out, or_1_out);
  buf buffer_3 (A_out, xor_2_out);

  // Notes on the sheet:
  //   Result
endmodule

module _4_Bit_Adder (
  input  B_3,
  input  B_2,
  input  B_1,
  input  B_0,
  input  A_3,
  input  A_2,
  input  A_1,
  input  A_0,
  input  C_In,
  output Out_3,
  output Out_2,
  output Out_1,
  output Out_0,
  output Out_C
);

  wire adder_1_c_out, adder_2_c_out, adder_3_c_out;

  adder adder_1 (._1(B_0), ._2(A_0), .C_in(C_In), .A_out(Out_0), .C_out(adder_1_c_out));
  adder adder_2 (._1(B_2), ._2(A_2), .C_in(adder_3_c_out), .A_out(Out_2), .C_out(adder_2_c_out));
  adder adder_3 (._1(B_1), ._2(A_1), .C_in(adder_1_c_out), .A_out(Out_1), .C_out(adder_3_c_out));
  adder adder_4 (._1(B_3), ._2(A_3), .C_in(adder_2_c_out), .A_out(Out_3), .C_out(Out_C));
endmodule

module _8_Bit_Adder_OLD (
  input  B_7,
  input  B_6,
  input  B_5,
  input  B_4,
  input  B_3,
  input  B_2,
  input  B_1,
  input  B_0,
  input  A_7,
  input  A_6,
  input  A_5,
  input  A_4,
  input  A_3,
  input  A_2,
  input  A_1,
  input  A_0,
  output Out_7,
  output Out_6,
  output Out_5,
  output Out_4,
  output Out_3,
  output Out_2,
  output Out_1,
  output Out_0
);

  wire n4_bit_adder_2_out_c;

  _4_Bit_Adder u_4_bit_adder_1 (
    .B_3(B_7), .B_2(B_6), .B_1(B_5), .B_0(B_4), .A_3(A_7), .A_2(A_6), .A_1(A_5), .A_0(A_4),
    .C_In(n4_bit_adder_2_out_c), .Out_3(Out_7), .Out_2(Out_6), .Out_1(Out_5), .Out_0(Out_4));  // open: Out_C
  _4_Bit_Adder u_4_bit_adder_2 (
    .B_3(B_3), .B_2(B_2), .B_1(B_1), .B_0(B_0), .A_3(A_3), .A_2(A_2), .A_1(A_1), .A_0(A_0), .C_In(1'b0),
    .Out_3(Out_3), .Out_2(Out_2), .Out_1(Out_1), .Out_0(Out_0), .Out_C(n4_bit_adder_2_out_c));
endmodule

module _8_Bit_Adder_Test (
  input  in_1,
  input  in_2,
  input  in_3,
  input  in_4,
  input  in_5,
  input  in_6,
  input  in_7,
  input  in_8,
  input  in_9,
  input  in_10,
  input  in_11,
  input  in_12,
  input  in_13,
  input  in_14,
  input  in_15,
  input  in_16
);

  wire n8_bit_adder_old_1_out_0, n8_bit_adder_old_1_out_1, n8_bit_adder_old_1_out_2,
       n8_bit_adder_old_1_out_3, n8_bit_adder_old_1_out_4, n8_bit_adder_old_1_out_5,
       n8_bit_adder_old_1_out_6, n8_bit_adder_old_1_out_7;

  _8_Bit_Adder_OLD u_8_bit_adder_old_1 (
    .B_7(in_1), .B_6(in_2), .B_5(in_3), .B_4(in_4), .B_3(in_5), .B_2(in_6), .B_1(in_7), .B_0(in_8),
    .A_7(in_9), .A_6(in_10), .A_5(in_11), .A_4(in_12), .A_3(in_13), .A_2(in_14), .A_1(in_15), .A_0(in_16),
    .Out_7(n8_bit_adder_old_1_out_7), .Out_6(n8_bit_adder_old_1_out_6), .Out_5(n8_bit_adder_old_1_out_5),
    .Out_4(n8_bit_adder_old_1_out_4), .Out_3(n8_bit_adder_old_1_out_3), .Out_2(n8_bit_adder_old_1_out_2),
    .Out_1(n8_bit_adder_old_1_out_1), .Out_0(n8_bit_adder_old_1_out_0));
  LED led_1 (.in(n8_bit_adder_old_1_out_7));
  LED led_2 (.in(n8_bit_adder_old_1_out_5));
  LED led_3 (.in(n8_bit_adder_old_1_out_6));
  LED led_4 (.in(n8_bit_adder_old_1_out_4));
  LED led_5 (.in(n8_bit_adder_old_1_out_1));
  LED led_6 (.in(n8_bit_adder_old_1_out_3));
  LED led_7 (.in(n8_bit_adder_old_1_out_2));
  LED led_8 (.in(n8_bit_adder_old_1_out_0));
endmodule

module _8_Bit_Adder (
  input  B_7,
  input  B_6,
  input  B_5,
  input  B_4,
  input  B_3,
  input  B_2,
  input  B_1,
  input  B_0,
  input  A_7,
  input  A_6,
  input  A_5,
  input  A_4,
  input  A_3,
  input  A_2,
  input  A_1,
  input  A_0,
  output Out_7,
  output Out_6,
  output Out_5,
  output Out_4,
  output Out_3,
  output Out_2,
  output Out_1,
  output Out_0
);

  wire adder_1_c_out, adder_2_c_out, adder_3_c_out, adder_4_c_out, adder_5_c_out, adder_6_c_out,
       adder_7_c_out, adder_8_c_out;

  adder adder_1 (._1(B_0), ._2(A_0), .C_in(1'b0), .A_out(Out_0), .C_out(adder_1_c_out));
  adder adder_2 (._1(B_2), ._2(A_2), .C_in(adder_3_c_out), .A_out(Out_2), .C_out(adder_2_c_out));
  adder adder_3 (._1(B_1), ._2(A_1), .C_in(adder_1_c_out), .A_out(Out_1), .C_out(adder_3_c_out));
  adder adder_4 (._1(B_4), ._2(A_4), .C_in(adder_5_c_out), .A_out(Out_4), .C_out(adder_4_c_out));
  adder adder_5 (._1(B_3), ._2(A_3), .C_in(adder_2_c_out), .A_out(Out_3), .C_out(adder_5_c_out));
  adder adder_6 (._1(B_6), ._2(A_6), .C_in(adder_7_c_out), .A_out(Out_6), .C_out(adder_6_c_out));
  adder adder_7 (._1(B_5), ._2(A_5), .C_in(adder_4_c_out), .A_out(Out_5), .C_out(adder_7_c_out));
  adder adder_8 (._1(B_7), ._2(A_7), .C_in(adder_6_c_out), .A_out(Out_7), .C_out(adder_8_c_out));
endmodule

module _8_Bit_Twos_Compliment (
  input  A_7,
  input  A_6,
  input  A_5,
  input  A_4,
  input  A_3,
  input  A_2,
  input  A_1,
  input  A_0,
  output Out_7,
  output Out_6,
  output Out_5,
  output Out_4,
  output Out_3,
  output Out_2,
  output Out_1,
  output Out_0
);

  wire not_1_out, not_2_out, not_3_out, not_4_out, not_5_out, not_6_out, not_7_out, not_8_out;

  not not_1 (not_1_out, A_7);
  not not_2 (not_2_out, A_6);
  not not_3 (not_3_out, A_5);
  not not_4 (not_4_out, A_4);
  not not_5 (not_5_out, A_3);
  not not_6 (not_6_out, A_2);
  not not_7 (not_7_out, A_1);
  not not_8 (not_8_out, A_0);
  _8_Bit_Adder u_8_bit_adder_1 (
    .B_7(1'b0), .B_6(1'b0), .B_5(1'b0), .B_4(1'b0), .B_3(1'b0), .B_2(1'b0), .B_1(1'b0), .B_0(1'b1),
    .A_7(not_1_out), .A_6(not_2_out), .A_5(not_3_out), .A_4(not_4_out), .A_3(not_5_out), .A_2(not_6_out),
    .A_1(not_7_out), .A_0(not_8_out), .Out_7(Out_7), .Out_6(Out_6), .Out_5(Out_5), .Out_4(Out_4),
    .Out_3(Out_3), .Out_2(Out_2), .Out_1(Out_1), .Out_0(Out_0));

  // Notes on the sheet:
  //   Two's Compliment, (Flip and Add One)
endmodule

module _8_Bit_ALU (
  input  in_1,
  input  in_2
);

  wire nand_1_out;

  nand nand_1 (nand_1_out, in_1, in_2);
endmodule

module _1_Bit_Selector (
  input  B,
  input  A,
  input  Selector,
  output Out
);

  wire and_1_out, and_2_out, not_1_out, not_2_out;

  not not_1 (not_1_out, not_2_out);
  not not_2 (not_2_out, Selector);
  and and_1 (and_1_out, B, not_1_out);
  or or_1 (Out, and_1_out, and_2_out);
  and and_2 (and_2_out, A, not_2_out);
endmodule

module _8_Bit_Selector (
  input  B_7,
  input  B_6,
  input  B_5,
  input  B_4,
  input  B_3,
  input  B_2,
  input  B_1,
  input  B_0,
  input  A_7,
  input  A_6,
  input  A_5,
  input  A_4,
  input  A_3,
  input  A_2,
  input  Selector,
  input  A_1,
  input  A_0,
  output Out_7,
  output Out_6,
  output Out_5,
  output Out_4,
  output Out_3,
  output Out_2,
  output Out_1,
  output Out_0
);

  _1_Bit_Selector u_1_bit_selector_1 (.B(B_7), .A(A_7), .Selector(Selector), .Out(Out_7));
  _1_Bit_Selector u_1_bit_selector_2 (.B(B_6), .A(A_6), .Selector(Selector), .Out(Out_6));
  _1_Bit_Selector u_1_bit_selector_3 (.B(B_5), .A(A_5), .Selector(Selector), .Out(Out_5));
  _1_Bit_Selector u_1_bit_selector_4 (.B(B_4), .A(A_4), .Selector(Selector), .Out(Out_4));
  _1_Bit_Selector u_1_bit_selector_5 (.B(B_3), .A(A_3), .Selector(Selector), .Out(Out_3));
  _1_Bit_Selector u_1_bit_selector_6 (.B(B_2), .A(A_2), .Selector(Selector), .Out(Out_2));
  _1_Bit_Selector u_1_bit_selector_7 (.B(B_1), .A(A_1), .Selector(Selector), .Out(Out_1));
  _1_Bit_Selector u_1_bit_selector_8 (.B(B_0), .A(A_0), .Selector(Selector), .Out(Out_0));
endmodule

module _1_Bit_Register (
  input  A,
  input  Set,
  output Out
);

  wire and_1_out, nor_1_out, nor_2_out;

  and and_1 (and_1_out, A, Set);
  nor nor_1 (nor_1_out, and_1_out, nor_2_out);
  nor nor_2 (nor_2_out, nor_1_out, Set);
  not not_1 (Out, nor_1_out);
endmodule

module _8_Bit_Register (
  input  in_1,
  input  in_2,
  input  in_3,
  input  in_4,
  input  in_5,
  input  in_6,
  input  in_7,
  input  in_8,
  input  in_9,
  output out_10,
  output out_11,
  output out_12,
  output out_13,
  output out_14,
  output out_15,
  output out_16,
  output out_17
);

  _1_Bit_Register u_1_bit_register_1 (.A(in_1), .Set(in_9), .Out(out_10));
  _1_Bit_Register u_1_bit_register_2 (.A(in_2), .Set(in_9), .Out(out_11));
  _1_Bit_Register u_1_bit_register_3 (.A(in_3), .Set(in_9), .Out(out_12));
  _1_Bit_Register u_1_bit_register_4 (.A(in_4), .Set(in_9), .Out(out_13));
  _1_Bit_Register u_1_bit_register_5 (.A(in_5), .Set(in_9), .Out(out_14));
  _1_Bit_Register u_1_bit_register_6 (.A(in_6), .Set(in_9), .Out(out_15));
  _1_Bit_Register u_1_bit_register_7 (.A(in_7), .Set(in_9), .Out(out_16));
  _1_Bit_Register u_1_bit_register_8 (.A(in_8), .Set(in_9), .Out(out_17));
endmodule

module _8_bit_RAM (
  input  in_1,
  input  in_2
);

  wire undriven, undriven_2, undriven_3, undriven_4, undriven_5, undriven_6, undriven_7, undriven_8;

  _1_Bit_Selector u_1_bit_selector_1 (.B(undriven), .A(undriven_2));  // open: Selector, Out
  _1_Bit_Selector u_1_bit_selector_2 (.B(undriven_3), .A(undriven_4));  // open: Selector, Out
  _1_Bit_Selector u_1_bit_selector_3 (.B(undriven_5), .A(undriven_6));  // open: Selector, Out
  _1_Bit_Selector u_1_bit_selector_4 (.B(undriven_7), .A(undriven_8));  // open: Selector, Out
endmodule

module _2_Bit_Decode (
  input  In_1,
  input  In_0,
  input  Decode,
  output Out_3,
  output Out_2,
  output Out_1,
  output Out_0
);

  wire and_1_out, and_2_out, and_3_out, and_4_out, not_1_out, not_2_out, not_3_out, not_4_out;

  not not_1 (not_1_out, In_1);
  not not_2 (not_2_out, In_0);
  not not_3 (not_3_out, not_1_out);
  not not_4 (not_4_out, not_2_out);
  and and_1 (and_1_out, not_4_out, not_3_out);
  and and_2 (and_2_out, not_2_out, not_3_out);
  and and_3 (and_3_out, not_1_out, not_4_out);
  and and_4 (and_4_out, not_2_out, not_1_out);
  and and_5 (Out_3, and_1_out, Decode);
  and and_6 (Out_2, and_2_out, Decode);
  and and_7 (Out_1, and_3_out, Decode);
  and and_8 (Out_0, and_4_out, Decode);
endmodule

module _4_Bit_Decode (
  input  In_3,
  input  In_2,
  input  In_1,
  input  In_0,
  input  Decode,
  output out_6,
  output out_7,
  output out_8,
  output out_9,
  output out_10,
  output out_11,
  output out_12,
  output out_13,
  output out_14,
  output out_15,
  output out_16,
  output out_17,
  output out_18,
  output out_19,
  output out_20,
  output out_21
);

  wire and_1_out, and_2_out, and_3_out, and_4_out, n2_bit_decode_1_out_0, n2_bit_decode_1_out_1,
       n2_bit_decode_1_out_2, n2_bit_decode_1_out_3, n2_bit_decode_2_out_0, n2_bit_decode_2_out_1,
       n2_bit_decode_2_out_2, n2_bit_decode_2_out_3, n2_bit_decode_3_out_0, n2_bit_decode_3_out_1,
       n2_bit_decode_3_out_2, n2_bit_decode_3_out_3, n2_bit_decode_4_out_0, n2_bit_decode_4_out_1,
       n2_bit_decode_4_out_2, n2_bit_decode_4_out_3, not_1_out, not_2_out;

  not not_1 (not_1_out, In_3);
  not not_2 (not_2_out, In_2);
  _2_Bit_Decode u_2_bit_decode_1 (
    .In_1(In_1), .In_0(In_0), .Decode(and_1_out), .Out_3(n2_bit_decode_1_out_3),
    .Out_2(n2_bit_decode_1_out_2), .Out_1(n2_bit_decode_1_out_1), .Out_0(n2_bit_decode_1_out_0));
  and and_1 (and_1_out, not_1_out, not_2_out);
  and and_2 (and_2_out, not_1_out, In_2);
  and and_3 (and_3_out, In_3, not_2_out);
  and and_4 (and_4_out, In_3, In_2);
  _2_Bit_Decode u_2_bit_decode_2 (
    .In_1(In_1), .In_0(In_0), .Decode(and_3_out), .Out_3(n2_bit_decode_2_out_3),
    .Out_2(n2_bit_decode_2_out_2), .Out_1(n2_bit_decode_2_out_1), .Out_0(n2_bit_decode_2_out_0));
  _2_Bit_Decode u_2_bit_decode_3 (
    .In_1(In_1), .In_0(In_0), .Decode(and_2_out), .Out_3(n2_bit_decode_3_out_3),
    .Out_2(n2_bit_decode_3_out_2), .Out_1(n2_bit_decode_3_out_1), .Out_0(n2_bit_decode_3_out_0));
  _2_Bit_Decode u_2_bit_decode_4 (
    .In_1(In_1), .In_0(In_0), .Decode(and_4_out), .Out_3(n2_bit_decode_4_out_3),
    .Out_2(n2_bit_decode_4_out_2), .Out_1(n2_bit_decode_4_out_1), .Out_0(n2_bit_decode_4_out_0));
  and and_5 (out_14, Decode, n2_bit_decode_3_out_3);
  and and_6 (out_15, Decode, n2_bit_decode_3_out_2);
  and and_7 (out_16, Decode, n2_bit_decode_3_out_1);
  and and_8 (out_17, Decode, n2_bit_decode_3_out_0);
  and and_9 (out_18, Decode, n2_bit_decode_1_out_3);
  and and_10 (out_19, Decode, n2_bit_decode_1_out_2);
  and and_11 (out_20, Decode, n2_bit_decode_1_out_1);
  and and_12 (out_21, Decode, n2_bit_decode_1_out_0);
  and and_13 (out_6, Decode, n2_bit_decode_4_out_3);
  and and_14 (out_7, Decode, n2_bit_decode_4_out_2);
  and and_15 (out_8, Decode, n2_bit_decode_4_out_1);
  and and_16 (out_9, Decode, n2_bit_decode_4_out_0);
  and and_17 (out_10, Decode, n2_bit_decode_2_out_3);
  and and_18 (out_11, Decode, n2_bit_decode_2_out_2);
  and and_19 (out_12, Decode, n2_bit_decode_2_out_1);
  and and_20 (out_13, Decode, n2_bit_decode_2_out_0);
endmodule
